// Digital circuit bcd_adder.dig as structural Verilog
module bcd_adder (
  input  [3:0] NumberA,
  input  [3:0] NumberB,
  input  syc,
  input  cin,
  output [3:0] N1,
  output coutt,
  output [3:0] N2
);

  wire and_1_out, and_2_out, and_3_out, fourbitadder_1_cout, fourbitadder_1_s0, fourbitadder_1_s1,
       fourbitadder_1_s2, fourbitadder_1_s3, or_1_out, or_2_out, or_3_out;
  wire [3:0] fourbitadder_2_s3;

  or or_1 (or_1_out, and_2_out, and_1_out, fourbitadder_1_cout);
  and and_1 (and_1_out, fourbitadder_1_s2, fourbitadder_1_s3);
  and and_2 (and_2_out, fourbitadder_1_s1, fourbitadder_1_s3);
  or or_2 (or_2_out, fourbitadder_1_cout, and_3_out);
  and and_3 (and_3_out, fourbitadder_1_s3, or_3_out);
  Multiplexer #(.Bits(4)) multiplexer_1 (.sel(syc), .in_0(NumberB), .in_1(fourbitadder_2_s3), .out(N2));
  or or_3 (or_3_out, fourbitadder_1_s1, fourbitadder_1_s2);
  fourbitadder fourbitadder_1 (
    .C_input(cin), .A0(NumberA[0]), .B0(NumberB[0]), .A1(NumberA[1]), .A2(NumberA[2]), .A3(NumberA[3]),
    .B1(NumberB[1]), .B2(NumberB[2]), .B3(NumberB[3]), .Cout(fourbitadder_1_cout), .S0(fourbitadder_1_s0),
    .S1(fourbitadder_1_s1), .S2(fourbitadder_1_s2), .S3(fourbitadder_1_s3));
  fourbitadder fourbitadder_2 (
    .C_input(1'b0), .A0(fourbitadder_1_s0), .B0(1'b0), .A1(fourbitadder_1_s1), .A2(fourbitadder_1_s2),
    .A3(fourbitadder_1_s3), .B1(or_1_out), .B2(or_1_out), .B3(1'b0), .S0(fourbitadder_2_s3[0]),
    .S1(fourbitadder_2_s3[1]), .S2(fourbitadder_2_s3[2]), .S3(fourbitadder_2_s3[3]));  // open: Cout
  Multiplexer #(.Bits(4)) multiplexer_2 (.sel(syc), .in_0(NumberA), .in_1(fourbitadder_2_s3), .out(N1));
  Multiplexer multiplexer_3 (.sel(syc), .in_0(cin), .in_1(or_2_out), .out(coutt));
endmodule
