// Digital circuit calculator.dig as structural Verilog
module calculator (
  input  [3:0] DATA,
  input  DA,
  input  CLK,
  output [3:0] D0,
  output [3:0] D1,
  output [3:0] D2,
  output [3:0] D3,
  output [3:0] D4,
  output [3:0] D5,
  output [3:0] D6,
  output [3:0] D7
);

  wire and_2_out, and_3_out, and_4_out, and_5_out, and_6_out, and_7_out, bcd_adder_1_coutt,
       bcd_adder_2_coutt, bcd_adder_3_coutt, bcd_adder_4_coutt, bcd_adder_5_coutt, bcd_adder_6_coutt,
       bcd_adder_7_coutt, d_ff_1_q, d_ff_2_q, not_1_out, not_2_out;
  wire [1:0] and_1_out;
  wire [3:0] bcd_adder_1_n1, bcd_adder_1_n2, bcd_adder_2_n1, bcd_adder_2_n2, bcd_adder_3_n1, bcd_adder_3_n2,
       bcd_adder_4_n1, bcd_adder_4_n2, bcd_adder_5_n1, bcd_adder_5_n2, bcd_adder_6_n1, bcd_adder_6_n2,
       bcd_adder_7_n1, bcd_adder_7_n2, bcd_adder_8_n1, bcd_adder_8_n2, d_ff_4_q, d_ff_6_q, d_ff_8_q,
       d_ff_10_q, d_ff_12_q, d_ff_14_q, d_ff_16_q, d_ff_18_q, multiplexer_1_out, multiplexer_2_out,
       multiplexer_3_out, multiplexer_4_out, multiplexer_5_out, multiplexer_6_out, multiplexer_7_out,
       multiplexer_8_out, multiplexer_9_out, multiplexer_10_out, multiplexer_11_out, multiplexer_12_out,
       multiplexer_13_out, multiplexer_14_out, multiplexer_15_out, multiplexer_16_out, multiplexer_17_out,
       multiplexer_18_out, multiplexer_19_out, multiplexer_20_out, multiplexer_21_out, multiplexer_22_out,
       multiplexer_23_out;

  or or_1 (and_1_out[0], and_3_out, and_2_out);
  and and_1 (and_1_out[1], and_5_out, and_4_out);
  and and_2 (and_2_out, and_5_out, and_4_out, DATA[0]);
  and and_3 (and_3_out, and_5_out, not_1_out);
  not not_1 (not_1_out, and_4_out);
  and and_4 (and_4_out, DATA[3], DATA[2], DATA[1]);
  and and_5 (and_5_out, DA, not_2_out);
  and and_6 (and_6_out, and_1_out[0], and_1_out[1]);
  not not_2 (not_2_out, d_ff_1_q);
  D_FF d_ff_1 (.D(DA), .C(CLK), .Q(d_ff_1_q));  // open: nQ
  and and_7 (and_7_out, DATA[0], DATA[1], DATA[2], DATA[3]);
  D_FF d_ff_2 (.D(and_7_out), .C(CLK), .Q(d_ff_2_q));  // open: nQ
  D_FF #(.Bits(4)) d_ff_3 (.D(multiplexer_2_out), .C(CLK), .Q(D0));  // open: nQ
  D_FF #(.Bits(4)) d_ff_4 (.D(multiplexer_1_out), .C(CLK), .Q(d_ff_4_q));  // open: nQ
  Multiplexer #(.Selector_Bits(2), .Bits(4)) multiplexer_1 (
    .sel(and_1_out), .in_0(bcd_adder_1_n2), .in_1(bcd_adder_1_n2), .in_2(4'b0000), .in_3(bcd_adder_1_n2),
    .out(multiplexer_1_out));
  Multiplexer #(.Selector_Bits(2), .Bits(4)) multiplexer_2 (
    .sel(and_1_out), .in_0(D0), .in_1(DATA), .in_2(4'b0000), .in_3(bcd_adder_1_n1), .out(multiplexer_2_out));
  bcd_adder bcd_adder_1 (
    .NumberA(D0), .NumberB(d_ff_4_q), .syc(and_6_out), .cin(1'b0), .N1(bcd_adder_1_n1),
    .coutt(bcd_adder_1_coutt), .N2(bcd_adder_1_n2));
  Multiplexer #(.Bits(4)) multiplexer_3 (.sel(d_ff_2_q), .in_0(D0), .in_1(4'b0000), .out(multiplexer_3_out));
  D_FF #(.Bits(4)) d_ff_5 (.D(multiplexer_5_out), .C(CLK), .Q(D1));  // open: nQ
  D_FF #(.Bits(4)) d_ff_6 (.D(multiplexer_4_out), .C(CLK), .Q(d_ff_6_q));  // open: nQ
  Multiplexer #(.Selector_Bits(2), .Bits(4)) multiplexer_4 (
    .sel(and_1_out), .in_0(bcd_adder_2_n2), .in_1(bcd_adder_2_n2), .in_2(4'b0000), .in_3(bcd_adder_2_n2),
    .out(multiplexer_4_out));
  bcd_adder bcd_adder_2 (
    .NumberA(D1), .NumberB(d_ff_6_q), .syc(and_6_out), .cin(bcd_adder_1_coutt), .N1(bcd_adder_2_n1),
    .coutt(bcd_adder_2_coutt), .N2(bcd_adder_2_n2));
  Multiplexer #(.Selector_Bits(2), .Bits(4)) multiplexer_5 (
    .sel(and_1_out), .in_0(D1), .in_1(multiplexer_3_out), .in_2(4'b0000), .in_3(bcd_adder_2_n1),
    .out(multiplexer_5_out));
  Multiplexer #(.Bits(4)) multiplexer_6 (.sel(d_ff_2_q), .in_0(D1), .in_1(4'b0000), .out(multiplexer_6_out));
  D_FF #(.Bits(4)) d_ff_7 (.D(multiplexer_8_out), .C(CLK), .Q(D2));  // open: nQ
  D_FF #(.Bits(4)) d_ff_8 (.D(multiplexer_7_out), .C(CLK), .Q(d_ff_8_q));  // open: nQ
  Multiplexer #(.Selector_Bits(2), .Bits(4)) multiplexer_7 (
    .sel(and_1_out), .in_0(bcd_adder_3_n2), .in_1(bcd_adder_3_n2), .in_2(4'b0000), .in_3(bcd_adder_3_n2),
    .out(multiplexer_7_out));
  Multiplexer #(.Selector_Bits(2), .Bits(4)) multiplexer_8 (
    .sel(and_1_out), .in_0(D2), .in_1(multiplexer_6_out), .in_2(4'b0000), .in_3(bcd_adder_3_n1),
    .out(multiplexer_8_out));
  bcd_adder bcd_adder_3 (
    .NumberA(D2), .NumberB(d_ff_8_q), .syc(and_6_out), .cin(bcd_adder_2_coutt), .N1(bcd_adder_3_n1),
    .coutt(bcd_adder_3_coutt), .N2(bcd_adder_3_n2));
  Multiplexer #(.Bits(4)) multiplexer_9 (.sel(d_ff_2_q), .in_0(D2), .in_1(4'b0000), .out(multiplexer_9_out));
  D_FF #(.Bits(4)) d_ff_9 (.D(multiplexer_12_out), .C(CLK), .Q(D3));  // open: nQ
  D_FF #(.Bits(4)) d_ff_10 (.D(multiplexer_10_out), .C(CLK), .Q(d_ff_10_q));  // open: nQ
  Multiplexer #(.Selector_Bits(2), .Bits(4)) multiplexer_10 (
    .sel(and_1_out), .in_0(bcd_adder_4_n2), .in_1(bcd_adder_4_n2), .in_2(4'b0000), .in_3(bcd_adder_4_n2),
    .out(multiplexer_10_out));
  bcd_adder bcd_adder_4 (
    .NumberA(D3), .NumberB(d_ff_10_q), .syc(and_6_out), .cin(bcd_adder_3_coutt), .N1(bcd_adder_4_n1),
    .coutt(bcd_adder_4_coutt), .N2(bcd_adder_4_n2));
  Multiplexer #(.Bits(4)) multiplexer_11 (.sel(d_ff_2_q), .in_0(D3), .in_1(4'b0000), .out(multiplexer_11_out));
  Multiplexer #(.Selector_Bits(2), .Bits(4)) multiplexer_12 (
    .sel(and_1_out), .in_0(D3), .in_1(multiplexer_9_out), .in_2(4'b0000), .in_3(bcd_adder_4_n1),
    .out(multiplexer_12_out));
  D_FF #(.Bits(4)) d_ff_11 (.D(multiplexer_14_out), .C(CLK), .Q(D4));  // open: nQ
  D_FF #(.Bits(4)) d_ff_12 (.D(multiplexer_13_out), .C(CLK), .Q(d_ff_12_q));  // open: nQ
  Multiplexer #(.Selector_Bits(2), .Bits(4)) multiplexer_13 (
    .sel(and_1_out), .in_0(bcd_adder_5_n2), .in_1(bcd_adder_5_n2), .in_2(4'b0000), .in_3(bcd_adder_5_n2),
    .out(multiplexer_13_out));
  Multiplexer #(.Selector_Bits(2), .Bits(4)) multiplexer_14 (
    .sel(and_1_out), .in_0(D4), .in_1(multiplexer_11_out), .in_2(4'b0000), .in_3(bcd_adder_5_n1),
    .out(multiplexer_14_out));
  bcd_adder bcd_adder_5 (
    .NumberA(D4), .NumberB(d_ff_12_q), .syc(and_6_out), .cin(bcd_adder_4_coutt), .N1(bcd_adder_5_n1),
    .coutt(bcd_adder_5_coutt), .N2(bcd_adder_5_n2));
  Multiplexer #(.Bits(4)) multiplexer_15 (.sel(d_ff_2_q), .in_0(D4), .in_1(4'b0000), .out(multiplexer_15_out));
  D_FF #(.Bits(4)) d_ff_13 (.D(multiplexer_18_out), .C(CLK), .Q(D5));  // open: nQ
  D_FF #(.Bits(4)) d_ff_14 (.D(multiplexer_16_out), .C(CLK), .Q(d_ff_14_q));  // open: nQ
  Multiplexer #(.Selector_Bits(2), .Bits(4)) multiplexer_16 (
    .sel(and_1_out), .in_0(bcd_adder_6_n2), .in_1(bcd_adder_6_n2), .in_2(4'b0000), .in_3(bcd_adder_6_n2),
    .out(multiplexer_16_out));
  bcd_adder bcd_adder_6 (
    .NumberA(D5), .NumberB(d_ff_14_q), .syc(and_6_out), .cin(bcd_adder_5_coutt), .N1(bcd_adder_6_n1),
    .coutt(bcd_adder_6_coutt), .N2(bcd_adder_6_n2));
  Multiplexer #(.Bits(4)) multiplexer_17 (.sel(d_ff_2_q), .in_0(D5), .in_1(4'b0000), .out(multiplexer_17_out));
  Multiplexer #(.Selector_Bits(2), .Bits(4)) multiplexer_18 (
    .sel(and_1_out), .in_0(D5), .in_1(multiplexer_15_out), .in_2(4'b0000), .in_3(bcd_adder_6_n1),
    .out(multiplexer_18_out));
  Multiplexer #(.Selector_Bits(2), .Bits(4)) multiplexer_19 (
    .sel(and_1_out), .in_0(bcd_adder_7_n2), .in_1(bcd_adder_7_n2), .in_2(4'b0000), .in_3(bcd_adder_7_n2),
    .out(multiplexer_19_out));
  D_FF #(.Bits(4)) d_ff_15 (.D(multiplexer_21_out), .C(CLK), .Q(D6));  // open: nQ
  D_FF #(.Bits(4)) d_ff_16 (.D(multiplexer_19_out), .C(CLK), .Q(d_ff_16_q));  // open: nQ
  Multiplexer #(.Bits(4)) multiplexer_20 (.sel(d_ff_2_q), .in_0(D6), .in_1(4'b0000), .out(multiplexer_20_out));
  Multiplexer #(.Selector_Bits(2), .Bits(4)) multiplexer_21 (
    .sel(and_1_out), .in_0(D6), .in_1(multiplexer_17_out), .in_2(4'b0000), .in_3(bcd_adder_7_n1),
    .out(multiplexer_21_out));
  bcd_adder bcd_adder_7 (
    .NumberA(D6), .NumberB(d_ff_16_q), .syc(and_6_out), .cin(bcd_adder_6_coutt), .N1(bcd_adder_7_n1),
    .coutt(bcd_adder_7_coutt), .N2(bcd_adder_7_n2));
  Multiplexer #(.Selector_Bits(2), .Bits(4)) multiplexer_22 (
    .sel(and_1_out), .in_0(bcd_adder_8_n2), .in_1(bcd_adder_8_n2), .in_2(4'b0000), .in_3(bcd_adder_8_n2),
    .out(multiplexer_22_out));
  D_FF #(.Bits(4)) d_ff_17 (.D(multiplexer_23_out), .C(CLK), .Q(D7));  // open: nQ
  D_FF #(.Bits(4)) d_ff_18 (.D(multiplexer_22_out), .C(CLK), .Q(d_ff_18_q));  // open: nQ
  Multiplexer #(.Selector_Bits(2), .Bits(4)) multiplexer_23 (
    .sel(and_1_out), .in_0(D7), .in_1(multiplexer_20_out), .in_2(4'b0000), .in_3(bcd_adder_8_n1),
    .out(multiplexer_23_out));
  bcd_adder bcd_adder_8 (
    .NumberA(D7), .NumberB(d_ff_18_q), .syc(and_6_out), .cin(bcd_adder_7_coutt), .N1(bcd_adder_8_n1),
    .N2(bcd_adder_8_n2));  // open: coutt
endmodule
